// Logisim project gtn.circ as structural Verilog: 5 circuits, main circuit main
module main (
  input  in_1,
  input  in_2,
  input  in_3,
  input  in_4,
  input  in_5,
  input  in_6,
  input  in_7,
  input  in_8
);

  wire a0_t, a1_t, a2_t, a3_t, a10, a11, a12, a13, A_JOGANDO, A_VENCEU, ACERTOU, and_2_out, and_3_out,
       and_6_out, and_7_out, and_10_out, and_11_out, and_12_out, and_21_out, and_24_out, and_28_out,
       and_29_out, and_30_out, and_31_out, and_34_out, and_35_out, and_36_out, and_37_out, and_38_out,
       and_40_out, and_45_out, and_46_out, and_47_out, and_49_out, and_56_out, and_57_out, and_58_out,
       and_61_out, and_62_out, and_63_out, and_65_out, and_67_out, and_69_out, and_71_out, and_73_out,
       and_74_out, and_75_out, and_77_out, b0_t, b1_t, b2_t, b3_t, b10, b11, b12, b13, B_JOGANDO, B_VENCEU,
       button_7_out, button_15_out, c0, c1, c2, c3, c10, c11, c12, c13, cfg, CHUTANDO_X, CHUTANDO_Y, CHUTAR,
       clk_0A, clk_0B, clk_1A, clk_1B, clk_1C, clk_1D, clk_2A, clk_3A, clock_1_out, clock_2_out,
       comparator_1_eq, comparator_2_eq, comparator_5_eq, comparator_5_gt, comparator_5_lt, configurar,
       configurar_t, d0, d1, d2, d3, d10, d11, d12, d13, d_ff_12_q, d_ff_12_qn, d_ff_14_q, d_ff_14_qn, dma_t,
       dmb_t, dsa_t, dsb_t, EMPATE, FIM_DE_JOGO, FIM_DE_JOGO_t, igual_x, jogando, MAIOR, MENOR, nor_1_out,
       not_1_out, not_2_out, or_1_out, or_2_out, or_4_out, or_5_out, or_6_out, or_8_out, or_10_out,
       or_15_out, or_16_out, or_17_out, or_18_out, or_20_out, or_22_out, or_23_out, or_24_out, or_26_out,
       or_27_out, or_28_out, or_30_out, or_32_out, or_33_out, or_34_out, or_35_out, \PRÓXIMO , reset, SA, SB,
       somador_sub_1_out_9, somador_sub_1_out_10, somador_sub_1_out_11, somador_sub_1_out_12,
       somador_sub_2_out_9, somador_sub_2_out_10, somador_sub_2_out_11, somador_sub_2_out_12, start, SX, SY,
       t_ff_1_q, t_ff_2_q, t_ff_4_q, turnout_a, turnout_b, uma_t, umb_t, usa_t, usb_t, verificando,
       xnor_1_out, xnor_2_out, xnor_3_out, xnor_4_out, zero_0, zero_01, zero_1, zero_2, zero_3, zero_11,
       zero_21, zero_31, zero_A, zero_AB, zero_B, zero_BB, zero_C, zero_CB, zero_D, zero_DB;
  wire [2:0] GA, GB, valor_x, valor_y;
  wire [3:0] adder_5_out, adder_6_out, DMA, DMB, DSA, DSB, or_11_out, PA, PB, random_1_out, random_2_out,
       UMA, UMB, undriven, undriven_2, USA, USB;

  D_Flip_Flop d_ff_1 (.clk(clk_3A), .D(d0), .Q(DMA[0]), .preset(zero_D), .reset(and_2_out));  // open: Qn
  or or_1 (or_1_out, zero_D, and_2_out);
  D_Flip_Flop d_ff_2 (.clk(clk_3A), .D(d1), .Q(DMA[1]), .reset(or_1_out));  // open: Qn, preset
  D_Flip_Flop d_ff_3 (.clk(clk_3A), .D(d2), .Q(DMA[2]), .preset(zero_D), .reset(and_2_out));  // open: Qn
  D_Flip_Flop d_ff_4 (.clk(clk_3A), .D(d3), .Q(DMA[3]), .reset(or_2_out));  // open: Qn, preset
  or or_2 (or_2_out, and_2_out, zero_D);
  and and_1 (zero_D, DMA[0], DMA[1], DMA[2], DMA[3]);
  Adder #(.width(4)) adder_1 (.a(DMA), .b(4'b1111), .out({d3, d2, d1, d0}));  // open: cin, cout
  and and_2 (and_2_out, cfg, reset);
  and and_3 (and_3_out, cfg, dma_t);
  and and_4 (zero_3, d0, d1, d2, d3);
  or or_3 (clk_3A, zero_C, and_3_out);
  Button button_1 (.out(uma_t));
  Button button_2 (.out(dma_t));
  Hex_Digit_Display hex_digit_display_1 (.value(UMA));  // open: dp
  Hex_Digit_Display hex_digit_display_2 (.value(DMA));  // open: dp
  LED led_1 (.in(SA));
  Hex_Digit_Display hex_digit_display_3 (.value(PA));  // open: dp
  Button button_3 (.out(dsa_t));
  Hex_Digit_Display hex_digit_display_4 (.value(DSA));  // open: dp
  Hex_Digit_Display hex_digit_display_5 (.value({1'b0, GA}));  // open: dp
  LED led_2 (.in(A_JOGANDO));
  D_Flip_Flop d_ff_5 (.clk(clk_2A), .D(c0), .Q(UMA[0]), .preset(or_4_out), .reset(and_7_out));  // open: Qn
  Button button_4 (.out(usa_t));
  Hex_Digit_Display hex_digit_display_6 (.value(USA));  // open: dp
  LED led_3 (.in(A_VENCEU));
  Button button_5 (.out(start));
  Button button_6 (.out(\PRÓXIMO ));
  LED led_4 (.in(SX));
  Button button_7 (.out(button_7_out));
  or or_4 (or_4_out, zero_C, button_7_out);
  D_Flip_Flop d_ff_6 (.clk(clk_2A), .D(c1), .Q(UMA[1]), .reset(or_5_out));  // open: Qn, preset
  or or_5 (or_5_out, or_4_out, and_7_out);
  LED led_5 (.in(FIM_DE_JOGO_t));
  LED led_6 (.in(EMPATE));
  LED led_7 (.in(cfg));
  Button button_8 (.out(configurar_t));
  LED led_8 (.in(ACERTOU));
  LED led_9 (.in(MAIOR));
  Hex_Digit_Display hex_digit_display_7 (.value({1'b0, valor_x}));  // open: dp
  LED led_10 (.in(CHUTANDO_X));
  or or_6 (or_6_out, and_7_out, or_4_out);
  LED led_11 (.in(MENOR));
  LED led_12 (.in(ACERTOU));
  LED led_13 (.in(SY));
  Hex_Digit_Display hex_digit_display_8 (.value({1'b0, valor_y}));  // open: dp
  D_Flip_Flop d_ff_7 (.clk(clk_2A), .D(c2), .Q(UMA[2]), .reset(or_6_out));  // open: Qn, preset
  LED led_14 (.in(B_VENCEU));
  Button button_9 (.out(reset));
  Button button_10 (.out(CHUTAR));
  LED led_15 (.in(CHUTANDO_Y));
  and and_5 (turnout_a, zero_0, zero_1, jogando, zero_2, zero_3);
  Button button_11 (.out(dmb_t));
  Hex_Digit_Display hex_digit_display_9 (.value(DMB));  // open: dp
  and and_6 (and_6_out, cfg, uma_t);
  D_Flip_Flop d_ff_8 (.clk(clk_2A), .D(c3), .Q(UMA[3]), .preset(or_4_out), .reset(and_7_out));  // open: Qn
  Hex_Digit_Display hex_digit_display_10 (.value(PB));  // open: dp
  Button button_12 (.out(umb_t));
  Hex_Digit_Display hex_digit_display_11 (.value(UMB));  // open: dp
  LED led_16 (.in(SB));
  Hex_Digit_Display hex_digit_display_12 (.value({1'b0, GB}));  // open: dp
  LED led_17 (.in(B_JOGANDO));
  or or_7 (clk_2A, zero_B, and_6_out);
  and and_7 (and_7_out, cfg, reset);
  and and_8 (zero_C, UMA[0], UMA[1], UMA[2], UMA[3]);
  Button button_13 (.out(usb_t));
  Button button_14 (.out(dsb_t));
  Hex_Digit_Display hex_digit_display_13 (.value(DSB));  // open: dp
  Hex_Digit_Display hex_digit_display_14 (.value(USB));  // open: dp
  Adder #(.width(4)) adder_2 (.a(UMA), .b(4'b1111), .out({c3, c2, c1, c0}));  // open: cin, cout
  and and_9 (zero_2, c0, c1, c2, c3);
  D_Flip_Flop d_ff_9 (.clk(clk_1A), .D(b0_t), .Q(DSA[0]), .preset(zero_B), .reset(and_21_out));  // open: Qn
  or or_8 (or_8_out, zero_B, and_21_out);
  D_Flip_Flop d_ff_10 (.clk(clk_1A), .D(b1_t), .Q(DSA[1]), .reset(or_8_out));  // open: Qn, preset
  and and_10 (and_10_out, \PRÓXIMO , verificando);
  and and_11 (and_11_out, cfg, dsa_t);
  D_Flip_Flop d_ff_11 (.clk(clk_1A), .D(b2_t), .Q(DSA[2]), .preset(zero_B), .reset(and_21_out));  // open: Qn
  D_Flip_Flop d_ff_12 (.clk(\PRÓXIMO ), .D(d_ff_14_q), .Q(d_ff_12_q), .Qn(d_ff_12_qn));  // open: preset, reset
  or or_9 (clk_1A, zero_A, and_11_out);
  or or_10 (or_10_out, and_21_out, zero_B);
  T_Flip_Flop t_ff_1 (.clk(and_10_out), .T(and_10_out), .Q(t_ff_1_q));  // open: Qn, preset, reset
  and and_12 (and_12_out, d_ff_14_qn, d_ff_12_qn);
  D_Flip_Flop d_ff_13 (.clk(clk_1A), .D(b3_t), .Q(DSA[3]), .reset(or_10_out));  // open: Qn, preset
  T_Flip_Flop t_ff_2 (.clk(not_1_out), .T(not_1_out), .Q(t_ff_2_q), .preset(turnout_a), .reset(turnout_b));  // open: Qn
  not not_1 (not_1_out, t_ff_1_q);
  and and_13 (GA[0], in_4, A_JOGANDO);
  and and_14 (GB[0], in_8, B_JOGANDO);
  and and_15 (GA[1], in_3, A_JOGANDO);
  and and_16 (GB[1], in_7, B_JOGANDO);
  and and_17 (GA[2], in_2, A_JOGANDO);
  and and_18 (GB[2], in_6, B_JOGANDO);
  and and_19 (SA, in_1, A_JOGANDO);
  and and_20 (SB, in_5, B_JOGANDO);
  Adder #(.width(4)) adder_3 (.a(DSA), .b(4'b1111), .out({b3_t, b2_t, b1_t, b0_t}));  // open: cin, cout
  and and_21 (and_21_out, cfg, reset);
  and and_22 (zero_B, DSA[0], DSA[1], DSA[2], DSA[3]);
  not not_2 (not_2_out, t_ff_2_q);
  D_Flip_Flop d_ff_14 (.clk(\PRÓXIMO ), .D(and_12_out), .Q(d_ff_14_q), .Qn(d_ff_14_qn));  // open: preset, reset
  and and_23 (A_JOGANDO, not_2_out, ~turnout_a);  // AND_Gate
  or or_11 (or_11_out[0], GA[0], GB[0]);
  or or_12 (or_11_out[1], GA[1], GB[1]);
  or or_13 (or_11_out[2], GA[2], GB[2]);
  or or_14 (or_11_out[3], SA, SB);
  and and_24 (and_24_out, ~d_ff_12_q, ~d_ff_14_q);  // AND_Gate
  and and_25 (B_JOGANDO, t_ff_2_q, ~turnout_b);  // AND_Gate
  and and_26 (verificando, ~d_ff_14_q, d_ff_12_q);  // AND_Gate
  and and_27 (zero_1, b0_t, b1_t, b2_t, b3_t);
  Register #(.width(4), .Select("low")) register_1 (
    .D(or_11_out), .Q({SX, valor_x}), .clk(and_28_out), .clr(and_31_out));  // open: en
  and and_28 (and_28_out, CHUTAR, ~verificando, and_24_out);  // AND_Gate
  Register #(.width(4), .Select("low")) register_2 (
    .D(or_11_out), .Q({SY, valor_y}), .clk(and_30_out), .clr(and_29_out));  // open: en
  and and_29 (and_29_out, reset, cfg);
  and and_30 (and_30_out, CHUTAR, ~verificando, d_ff_14_q);  // AND_Gate
  D_Flip_Flop d_ff_15 (.clk(clk_0A), .D(a0_t), .Q(USA[0]), .preset(zero_A), .reset(and_40_out));  // open: Qn
  and and_31 (and_31_out, reset, cfg);
  and and_32 (CHUTANDO_X, and_24_out, ~verificando);  // AND_Gate
  and and_33 (CHUTANDO_Y, d_ff_14_q, ~verificando);  // AND_Gate
  or or_15 (or_15_out, configurar, start);
  D_Flip_Flop d_ff_16 (.clk(clk_0A), .D(a1_t), .Q(USA[1]), .reset(or_16_out));  // open: Qn, preset
  or or_16 (or_16_out, zero_A, and_40_out);
  T_Flip_Flop t_ff_3 (.clk(or_15_out), .T(or_15_out), .Q(cfg));  // open: Qn, preset, reset
  or or_17 (or_17_out, and_40_out, zero_A);
  D_Flip_Flop d_ff_17 (.clk(clk_0A), .D(a2_t), .Q(USA[2]), .reset(or_17_out));  // open: Qn, preset
  and and_34 (and_34_out, A_JOGANDO, ~turnout_a);  // AND_Gate
  somador_sub somador_sub_1 (
    .a0(valor_x[0]), .b0(valor_y[0]), .a1(valor_x[1]), .b1(valor_y[1]), .a2(valor_x[2]), .b2(valor_y[2]),
    .a3(SX), .b3(SY), .out_9(somador_sub_1_out_9), .out_10(somador_sub_1_out_10),
    .out_11(somador_sub_1_out_11), .out_12(somador_sub_1_out_12));
  and and_35 (and_35_out, turnout_a, turnout_b);
  Comparator #(.width(4)) comparator_1 (.a(PA), .b(4'b1111), .eq(comparator_1_eq));  // open: gt, lt
  Comparator #(.width(4)) comparator_2 (.a(PB), .b(4'b1111), .eq(comparator_2_eq));  // open: gt, lt
  and and_36 (and_36_out, cfg, usa_t);
  Clock clock_1 (.out(clock_1_out));
  and and_37 (and_37_out, clock_1_out, t_ff_4_q);
  T_Flip_Flop t_ff_4 (.clk(and_34_out), .T(and_34_out), .Q(t_ff_4_q), .preset(start), .reset(or_18_out));  // open: Qn
  or or_18 (or_18_out, B_JOGANDO, cfg, FIM_DE_JOGO_t, turnout_a);
  D_Flip_Flop d_ff_18 (.clk(clk_0A), .D(a3_t), .Q(USA[3]), .preset(zero_A), .reset(and_40_out));  // open: Qn
  Random #(.width(4), .seed(3)) random_1 (.clk(\PRÓXIMO ), .next(ACERTOU), .out(random_1_out));  // open: clr
  Random #(.width(4), .seed(2)) random_2 (.clk(\PRÓXIMO ), .next(ACERTOU), .out(random_2_out));  // open: clr
  or or_19 (FIM_DE_JOGO, and_35_out, or_20_out);
  or or_20 (or_20_out, comparator_1_eq, comparator_2_eq);
  and and_38 (and_38_out, cfg, reset);
  and and_39 (zero_A, USA[0], USA[1], USA[2], USA[3]);
  Comparator #(.width(4)) comparator_3 (.a({SY, valor_y}), .b(undriven));  // open: gt, eq, lt
  or or_21 (clk_0A, and_36_out, and_37_out);
  S_R_Flip_Flop s_r_ff_1 (.Q(jogando), .preset(t_ff_4_q), .reset(and_38_out));  // open: S, clk, R, Qn
  Adder #(.width(4)) adder_4 (.a(USA), .b(4'b1111), .out({a3_t, a2_t, a1_t, a0_t}));  // open: cin, cout
  and and_40 (and_40_out, cfg, reset);
  Comparator #(.width(4)) comparator_4 (.a({SX, valor_x}), .b(undriven_2));  // open: gt, eq, lt
  // AND_Gate and_41 has open pins: in0=verificando, out=open
  // AND_Gate and_42 has open pins: in0=igual_x, out=open
  // AND_Gate and_43 has open pins: in0=verificando, out=open
  somador_sub somador_sub_2 (
    .a0(random_1_out[0]), .b0(random_2_out[0]), .a1(random_1_out[1]), .b1(random_2_out[1]),
    .a2(random_1_out[2]), .b2(random_2_out[2]), .a3(random_1_out[3]), .b3(random_2_out[3]),
    .out_9(somador_sub_2_out_9), .out_10(somador_sub_2_out_10), .out_11(somador_sub_2_out_11),
    .out_12(somador_sub_2_out_12));
  and and_44 (zero_0, a0_t, a1_t, a2_t, a3_t);
  xnor xnor_1 (xnor_1_out, somador_sub_1_out_9, somador_sub_2_out_9);
  xnor xnor_2 (xnor_2_out, somador_sub_1_out_10, somador_sub_2_out_10);
  xnor xnor_3 (xnor_3_out, somador_sub_1_out_11, somador_sub_2_out_11);
  xnor xnor_4 (xnor_4_out, somador_sub_1_out_12, somador_sub_2_out_12);
  and and_45 (and_45_out, somador_sub_1_out_9, ~somador_sub_2_out_9);  // AND_Gate
  and and_46 (and_46_out, xnor_1_out, somador_sub_1_out_10, ~somador_sub_2_out_10);  // AND_Gate
  and and_47 (and_47_out, xnor_1_out, xnor_2_out, somador_sub_1_out_9, ~somador_sub_2_out_9);  // AND_Gate
  and and_48 (and_47_out, xnor_1_out, xnor_2_out, xnor_3_out, somador_sub_1_out_9, ~somador_sub_2_out_9);  // AND_Gate
  Comparator #(.width(4)) comparator_5 (
    .a(PA), .b(PB), .gt(comparator_5_gt), .eq(comparator_5_eq), .lt(comparator_5_lt));
  and and_49 (and_49_out, xnor_1_out, xnor_2_out, xnor_3_out, xnor_4_out);
  or or_22 (or_22_out, and_45_out, and_46_out, and_47_out, and_47_out);
  and and_50 (A_VENCEU, FIM_DE_JOGO, comparator_5_gt);
  and and_51 (EMPATE, comparator_5_eq, FIM_DE_JOGO);
  and and_52 (B_VENCEU, comparator_5_lt, FIM_DE_JOGO);
  nor nor_1 (nor_1_out, and_49_out, or_22_out);
  D_Flip_Flop d_ff_19 (.clk(clk_1D), .D(d10), .Q(DMB[0]), .preset(zero_DB), .reset(and_62_out));  // open: Qn
  and and_53 (ACERTOU, and_49_out, verificando);
  and and_54 (MENOR, nor_1_out, verificando);
  and and_55 (MAIOR, or_22_out, verificando);
  D_Flip_Flop d_ff_20 (.clk(clk_1D), .D(d11), .Q(DMB[1]), .reset(or_23_out));  // open: Qn, preset
  or or_23 (or_23_out, zero_DB, and_62_out);
  D_Flip_Flop d_ff_21 (.clk(clk_1D), .D(d12), .Q(DMB[2]), .preset(zero_DB), .reset(and_62_out));  // open: Qn
  Register #(.width(4), .Select("low")) register_3 (
    .D(adder_5_out), .Q(PA), .clk(and_56_out), .clr(and_58_out));  // open: en
  and and_56 (and_56_out, A_JOGANDO, ACERTOU);
  and and_57 (and_57_out, B_JOGANDO, ACERTOU);
  D_Flip_Flop d_ff_22 (.clk(clk_1D), .D(d13), .Q(DMB[3]), .reset(or_24_out));  // open: Qn, preset
  or or_24 (or_24_out, and_62_out, zero_DB);
  and and_58 (and_58_out, cfg, reset);
  Register #(.width(4), .Select("low")) register_4 (
    .D(adder_6_out), .Q(PB), .clk(and_57_out), .clr(and_61_out));  // open: en
  and and_59 (zero_DB, DMB[0], DMB[1], DMB[2], DMB[3]);
  and and_60 (turnout_b, zero_01, zero_11, zero_21, zero_31);
  Adder #(.width(4)) adder_5 (.a(PA), .b(4'b0001), .out(adder_5_out));  // open: cin, cout
  Adder #(.width(4)) adder_6 (.a(PB), .b(4'b0001), .out(adder_6_out));  // open: cin, cout
  and and_61 (and_61_out, cfg, reset);
  Adder #(.width(4)) adder_7 (.a(DMB), .b(4'b1111), .out({d13, d12, d11, d10}));  // open: cin, cout
  and and_62 (and_62_out, cfg, reset);
  and and_63 (and_63_out, cfg, dmb_t);
  or or_25 (clk_1D, zero_CB, and_63_out);
  and and_64 (zero_31, d10, d11, d12, d13);
  D_Flip_Flop d_ff_23 (.clk(clk_1C), .D(c10), .Q(UMB[0]), .preset(or_27_out), .reset(and_67_out));  // open: Qn
  or or_26 (or_26_out, or_27_out, and_67_out);
  Button button_15 (.out(button_15_out));
  or or_27 (or_27_out, zero_CB, button_15_out);
  D_Flip_Flop d_ff_24 (.clk(clk_1C), .D(c11), .Q(UMB[1]), .reset(or_26_out));  // open: Qn, preset
  D_Flip_Flop d_ff_25 (.clk(clk_1C), .D(c12), .Q(UMB[2]), .reset(or_28_out));  // open: Qn, preset
  or or_28 (or_28_out, and_67_out, or_27_out);
  D_Flip_Flop d_ff_26 (.clk(clk_1C), .D(c13), .Q(UMB[3]), .preset(or_27_out), .reset(and_67_out));  // open: Qn
  or or_29 (clk_1C, zero_BB, and_65_out);
  and and_65 (and_65_out, cfg, umb_t);
  and and_66 (zero_CB, UMB[0], UMB[1], UMB[2], UMB[3]);
  Adder #(.width(4)) adder_8 (.a(UMB), .b(4'b1111), .out({c13, c12, c11, c10}));  // open: cin, cout
  and and_67 (and_67_out, cfg, reset);
  D_Flip_Flop d_ff_27 (.clk(clk_1B), .D(b10), .Q(DSB[0]), .preset(zero_BB), .reset(and_71_out));  // open: Qn
  and and_68 (zero_21, c10, c11, c12, c13);
  D_Flip_Flop d_ff_28 (.clk(clk_1B), .D(b11), .Q(DSB[1]), .reset(or_30_out));  // open: Qn, preset
  or or_30 (or_30_out, zero_BB, and_71_out);
  D_Flip_Flop d_ff_29 (.clk(clk_1B), .D(b12), .Q(DSB[2]), .preset(zero_BB), .reset(and_71_out));  // open: Qn
  and and_69 (and_69_out, cfg, dsb_t);
  or or_31 (clk_1B, zero_AB, and_69_out);
  D_Flip_Flop d_ff_30 (.clk(clk_1B), .D(b13), .Q(DSB[3]), .reset(or_32_out));  // open: Qn, preset
  or or_32 (or_32_out, and_71_out, zero_BB);
  and and_70 (zero_BB, DSB[0], DSB[1], DSB[2], DSB[3]);
  Adder #(.width(4)) adder_9 (.a(DSB), .b(4'b1111), .out({b13, b12, b11, b10}));  // open: cin, cout
  and and_71 (and_71_out, cfg, reset);
  and and_72 (zero_11, b10, b11, b12, b13);
  D_Flip_Flop d_ff_31 (.clk(clk_0B), .D(a10), .Q(USB[0]), .preset(zero_AB), .reset(and_77_out));  // open: Qn
  or or_33 (or_33_out, zero_AB, and_77_out);
  or or_34 (or_34_out, configurar, start);
  D_Flip_Flop d_ff_32 (.clk(clk_0B), .D(a11), .Q(USB[1]), .reset(or_33_out));  // open: Qn, preset
  T_Flip_Flop t_ff_5 (.clk(or_34_out), .T(or_34_out), .Q(cfg));  // open: Qn, preset, reset
  D_Flip_Flop d_ff_33 (.clk(clk_0B), .D(a12), .Q(USB[2]), .reset(or_35_out));  // open: Qn, preset
  or or_35 (or_35_out, and_77_out, zero_AB);
  Clock clock_2 (.out(clock_2_out));
  and and_73 (and_73_out, B_JOGANDO, ~cfg, ~FIM_DE_JOGO_t);  // AND_Gate
  D_Flip_Flop d_ff_34 (.clk(clk_0B), .D(a13), .Q(USB[3]), .preset(zero_AB), .reset(and_77_out));  // open: Qn
  and and_74 (and_74_out, cfg, usb_t);
  and and_75 (and_75_out, clock_2_out, and_73_out);
  and and_76 (zero_AB, USB[0], USB[1], USB[2], USB[3]);
  or or_36 (clk_0B, and_74_out, and_75_out);
  and and_77 (and_77_out, cfg, reset);
  Adder #(.width(4)) adder_10 (.a(USB), .b(4'b1111), .out({a13, a12, a11, a10}));  // open: cin, cout
  and and_78 (zero_01, a10, a11, a12, a13);

  // Other names for the same wires on the sheet: A0 = in_4; A1 = in_3; A2 = in_2; A3 = in_1; B0 = in_8; B1 = in_7;
  //   B2 = in_6; B3 = in_5; IGUAL = ACERTOU; valor_x[3] = SX; valor_y[3] = SY; XH[2:0] = valor_x; YH[2:0] = valor_y

  // Notes on the sheet:
  //   CRONÔMETRO A
  //   Turnout A
  //   CRONÔMETRO B
  //   cronomêtro A
  //   Alternar entre jogador A e B
  //   Alternar entre inputs de jogadores 
  //   Somador das coordenas
  //   gerar valor aleatório
  //   FIM DO JOGO
  //   FIM DO JOGO
  //   Comparar com o número aleatório gerado
  //   COMPARAR PLACAR
  //   Resultado
  //   igual
  //   menor
  //   maior
  //   PLACAR A
  //   PLACAR B
  //   Turnout B
  //   cronomêtro B
endmodule

module halfadder (
  input  in_1,
  input  in_2,
  output s,
  output c0
);

  and and_1 (c0, in_1, in_2);
  xor xor_1 (s, in_1, in_2);
endmodule

module fulladder (
  input  in_1,
  input  in_2,
  input  in_3,
  output out_4,
  output out_5
);

  wire halfadder_1_c0, halfadder_1_s, halfadder_2_c0;

  halfadder halfadder_1 (.in_1(in_2), .in_2(in_3), .s(halfadder_1_s), .c0(halfadder_1_c0));
  halfadder halfadder_2 (.in_1(in_1), .in_2(halfadder_1_s), .s(out_4), .c0(halfadder_2_c0));
  or or_1 (out_5, halfadder_2_c0, halfadder_1_c0);
endmodule

module somador_sub (
  input  a0,
  input  b0,
  input  a1,
  input  b1,
  input  a2,
  input  b2,
  input  a3,
  input  b3,
  output out_9,
  output out_10,
  output out_11,
  output out_12
);

  wire fulladder_1_out_5, fulladder_2_out_5, fulladder_3_out_5, or_1_out, xor_1_out, xor_2_out, xor_3_out,
       xor_4_out, xor_5_out, xor_6_out;

  xor xor_1 (xor_1_out, a0, a3);
  xor xor_2 (xor_2_out, b3, b0);
  xor xor_3 (xor_3_out, a1, a3);
  xor xor_4 (xor_4_out, b3, b1);
  xor xor_5 (xor_5_out, a2, a3);
  xor xor_6 (xor_6_out, b3, b2);
  or or_1 (or_1_out, a3, b3);
  fulladder fulladder_1 (.in_1(or_1_out), .in_2(xor_1_out), .in_3(xor_2_out), .out_4(out_9), .out_5(fulladder_1_out_5));
  fulladder fulladder_2 (
    .in_1(fulladder_1_out_5), .in_2(xor_3_out), .in_3(xor_4_out), .out_4(out_10), .out_5(fulladder_2_out_5));
  fulladder fulladder_3 (
    .in_1(fulladder_2_out_5), .in_2(xor_5_out), .in_3(xor_6_out), .out_4(out_11), .out_5(fulladder_3_out_5));
  fulladder fulladder_4 (.in_1(fulladder_3_out_5), .in_2(a3), .in_3(b3), .out_4(out_12));  // open: out_5
endmodule

module GAME (
  input  in_1,
  input  in_2,
  input  in_3,
  input  in_4,
  input  in_5,
  input  in_6,
  input  in_7,
  input  in_8,
  input  in_9,
  output igual,
  output menor,
  output maior
);

  wire and_1_out, and_2_out, and_3_out, and_5_out, nor_1_out, or_1_out, xnor_1_out, xnor_2_out, xnor_3_out,
       xnor_4_out;

  xnor xnor_1 (xnor_1_out, in_2, in_3);
  xnor xnor_2 (xnor_2_out, in_5, in_4);
  xnor xnor_3 (xnor_3_out, in_8, in_6);
  xnor xnor_4 (xnor_4_out, in_9, in_7);
  and and_1 (and_1_out, in_2, ~in_3);  // AND_Gate
  and and_2 (and_2_out, xnor_1_out, in_5, ~in_4);  // AND_Gate
  and and_3 (and_3_out, xnor_1_out, xnor_2_out, in_2, ~in_3);  // AND_Gate
  and and_4 (and_3_out, xnor_1_out, xnor_2_out, xnor_3_out, in_2, ~in_3);  // AND_Gate
  and and_5 (and_5_out, xnor_1_out, xnor_2_out, xnor_3_out, xnor_4_out);
  or or_1 (or_1_out, and_1_out, and_2_out, and_3_out, and_3_out);
  nor nor_1 (nor_1_out, and_5_out, or_1_out);
  and and_6 (igual, and_5_out, in_1);
  and and_7 (menor, nor_1_out, in_1);
  and and_8 (maior, or_1_out, in_1);
endmodule
